// Logisim project orga (1).circ as structural Verilog: 9 circuits, main circuit main
module main (
  input  [7:0] in_1,
  output [3:0] centena,
  output [3:0] decena,
  output [3:0] Unidad
);

  wire n7447_1_out_5, n7447_1_out_6, n7447_1_out_7, n7447_1_out_8, n7447_1_out_9, n7447_1_out_10,
       n7447_1_out_11, n7447_2_out_5, n7447_2_out_6, n7447_2_out_7, n7447_2_out_8, n7447_2_out_9,
       n7447_2_out_10, n7447_2_out_11, n7447_3_out_5, n7447_3_out_6, n7447_3_out_7, n7447_3_out_8,
       n7447_3_out_9, n7447_3_out_10, n7447_3_out_11;

  ROM #(.dataWidth(4)) rom_1 (.addr(in_1), .data(centena));  // open: sel
  ROM #(.dataWidth(4)) rom_2 (.addr(in_1), .data(decena));  // open: sel
  ROM #(.dataWidth(4)) rom_3 (.addr(in_1), .data(Unidad));  // open: sel
  _7447 u_7447_1 (
    .A(centena[3]), .B(centena[2]), .C(centena[1]), .D(centena[0]), .out_5(n7447_1_out_5),
    .out_6(n7447_1_out_6), .out_7(n7447_1_out_7), .out_8(n7447_1_out_8), .out_9(n7447_1_out_9),
    .out_10(n7447_1_out_10), .out_11(n7447_1_out_11));
  _7447 u_7447_2 (
    .A(decena[3]), .B(decena[2]), .C(decena[1]), .D(decena[0]), .out_5(n7447_2_out_5), .out_6(n7447_2_out_6),
    .out_7(n7447_2_out_7), .out_8(n7447_2_out_8), .out_9(n7447_2_out_9), .out_10(n7447_2_out_10),
    .out_11(n7447_2_out_11));
  _7_Segment_Display u_7_segment_display_1 (
    .g(n7447_1_out_11), .f(n7447_1_out_10), .a(n7447_1_out_5), .b(n7447_1_out_6), .e(n7447_1_out_9),
    .d(n7447_1_out_8), .c(n7447_1_out_7));  // open: dp
  _7_Segment_Display u_7_segment_display_2 (
    .g(n7447_2_out_11), .f(n7447_2_out_10), .a(n7447_2_out_5), .b(n7447_2_out_6), .e(n7447_2_out_9),
    .d(n7447_2_out_8), .c(n7447_2_out_7));  // open: dp
  _7447 u_7447_3 (
    .A(Unidad[3]), .B(Unidad[2]), .C(Unidad[1]), .D(Unidad[0]), .out_5(n7447_3_out_5), .out_6(n7447_3_out_6),
    .out_7(n7447_3_out_7), .out_8(n7447_3_out_8), .out_9(n7447_3_out_9), .out_10(n7447_3_out_10),
    .out_11(n7447_3_out_11));
  _7_Segment_Display u_7_segment_display_3 (
    .g(n7447_3_out_11), .f(n7447_3_out_10), .a(n7447_3_out_5), .b(n7447_3_out_6), .e(n7447_3_out_9),
    .d(n7447_3_out_8), .c(n7447_3_out_7));  // open: dp

  // Notes on the sheet:
  //   ROM
  //   CENTENA
  //   DECENEA
  //   UNIDAD
  //   contents of rom_1 (hex, n*v repeats v):
  //   100*0 100*1 56*2
  //   contents of rom_2 (hex, n*v repeats v):
  //   10*0 10*1 10*2 10*3 10*4 10*5 10*6 10*7 10*8 10*9 10*0 10*1 10*2 10*3 10*4 10*5 10*6 10*7 10*8 10*9
  //   10*0 10*1 10*2 10*3 10*4 6*5
  //   contents of rom_3 (hex, n*v repeats v):
  //   0 1 2 3 4 5 6 7 8 9 0 1 2 3 4 5 6 7 8 9 0 1 2 3 4 5 6 7 8 9 0 1 2 3 4 5 6 7 8 9 0 1 2 3 4 5 6 7 8 9
  //   0 1 2 3 4 5 6 7 8 9 0 1 2 3 4 5 6 7 8 9 0 1 2 3 4 5 6 7 8 9 0 1 2 3 4 5 6 7 8 9 0 1 2 3 4 5 6 7 8 9
  //   0 1 2 3 4 5 6 7 8 9 0 1 2 3 4 5 6 7 8 9 0 1 2 3 4 5 6 7 8 9 0 1 2 3 4 5 6 7 8 9 0 1 2 3 4 5 6 7 8 9
  //   0 1 2 3 4 5 6 7 8 9 0 1 2 3 4 5 6 7 8 9 0 1 2 3 4 5 6 7 8 9 0 1 2 3 4 5 6 7 8 9 0 1 2 3 4 5 6 7 8 9
  //   0 1 2 3 4 5 6 7 8 9 0 1 2 3 4 5 6 7 8 9 0 1 2 3 4 5 6 7 8 9 0 1 2 3 4 5 6 7 8 9 0 1 2 3 4 5 6 7 8 9
  //   0 1 2 3 4 5
  //   INPUT
  //   8 bits
  //   7447
  //   7447
  //   BCD 4 bits
  //   7447
endmodule

module LedA (
  input  A,
  input  B,
  input  C,
  input  D,
  output out_5
);

  wire A_B_prime_C_prime_out, A_prime_B_D_out, A_prime_B_prime_D_prime_out, A_prime_C_out;

  and A_prime_C (A_prime_C_out, ~A, C);  // AND_Gate
  and A_prime_B_prime_D_prime (A_prime_B_prime_D_prime_out, ~A, ~B, ~D);  // AND_Gate
  and A_prime_B_D (A_prime_B_D_out, ~A, B, D);  // AND_Gate
  and A_B_prime_C_prime (A_B_prime_C_prime_out, A, ~B, ~C);  // AND_Gate
  or or_1 (out_5, A_prime_C_out, A_prime_B_prime_D_prime_out, A_prime_B_D_out, A_B_prime_C_prime_out);
endmodule

module LedB (
  input  A,
  input  B,
  input  C,
  input  D,
  output out_5
);

  wire A_prime_B_prime_out, A_prime_C_D_out, A_prime_C_prime_D_prime_out, B_prime_C_prime_out;

  and A_prime_B_prime (A_prime_B_prime_out, ~A, ~B);  // AND_Gate
  and B_prime_C_prime (B_prime_C_prime_out, ~B, ~C);  // AND_Gate
  and A_prime_C_D (A_prime_C_D_out, ~A, C, D);  // AND_Gate
  and A_prime_C_prime_D_prime (A_prime_C_prime_D_prime_out, ~A, ~C, ~D);  // AND_Gate
  or or_1 (out_5, A_prime_B_prime_out, B_prime_C_prime_out, A_prime_C_D_out, A_prime_C_prime_D_prime_out);
endmodule

module LedC (
  input  A,
  input  B,
  input  C,
  input  D,
  output out_5
);

  wire A_prime_B_out, B_prime_C_prime_out, B_prime_D_out;

  and A_prime_B (A_prime_B_out, ~A, B);  // AND_Gate
  and B_prime_C_prime (B_prime_C_prime_out, ~B, ~C);  // AND_Gate
  and B_prime_D (B_prime_D_out, ~B, D);  // AND_Gate
  or or_1 (out_5, A_prime_B_out, B_prime_C_prime_out, B_prime_D_out);
endmodule

module LedD (
  input  A,
  input  B,
  input  C,
  input  D,
  output out_5
);

  wire A_prime_B_C_prime_D_out, A_prime_B_prime_C_out, A_prime_C_D_prime_out, B_prime_C_prime_D_prime_out;

  and B_prime_C_prime_D_prime (B_prime_C_prime_D_prime_out, ~B, ~C, ~D);  // AND_Gate
  and A_prime_B_C_prime_D (A_prime_B_C_prime_D_out, ~A, B, ~C, D);  // AND_Gate
  and A_prime_B_prime_C (A_prime_B_prime_C_out, ~A, ~B, C);  // AND_Gate
  and A_prime_C_D_prime (A_prime_C_D_prime_out, ~A, C, ~D);  // AND_Gate
  or or_1 (out_5, B_prime_C_prime_D_prime_out, A_prime_B_C_prime_D_out, A_prime_B_prime_C_out, A_prime_C_D_prime_out);
endmodule

module LedE (
  input  A,
  input  B,
  input  C,
  input  D,
  output out_5
);

  wire A_prime_C_D_prime_out, B_prime_C_prime_D_prime_out;

  and B_prime_C_prime_D_prime (B_prime_C_prime_D_prime_out, ~B, ~C, ~D);  // AND_Gate
  and A_prime_C_D_prime (A_prime_C_D_prime_out, ~A, C, ~D);  // AND_Gate
  or or_1 (out_5, B_prime_C_prime_D_prime_out, A_prime_C_D_prime_out);
endmodule

module LedF (
  input  A,
  input  B,
  input  C,
  input  D,
  output out_5
);

  wire A_B_prime_C_prime_out, A_prime_B_C_prime_out, A_prime_B_D_prime_out, A_prime_C_prime_D_prime_out;

  and A_prime_C_prime_D_prime (A_prime_C_prime_D_prime_out, ~A, ~C, ~D);  // AND_Gate
  and A_prime_B_C_prime (A_prime_B_C_prime_out, ~A, B, ~C);  // AND_Gate
  and A_prime_B_D_prime (A_prime_B_D_prime_out, ~A, B, ~D);  // AND_Gate
  and A_B_prime_C_prime (A_B_prime_C_prime_out, A, ~B, ~C);  // AND_Gate
  or or_1 (out_5, A_prime_C_prime_D_prime_out, A_prime_B_C_prime_out, A_prime_B_D_prime_out, A_B_prime_C_prime_out);
endmodule

module LedG (
  input  A,
  input  B,
  input  C,
  input  D,
  output out_5
);

  wire A_B_prime_C_prime_out, A_prime_B_C_prime_out, A_prime_B_prime_C_out, A_prime_C__D_prime_out;

  and A_prime_B_prime_C (A_prime_B_prime_C_out, ~A, ~B, C);  // AND_Gate
  and A_prime_B_C_prime (A_prime_B_C_prime_out, ~A, B, ~C);  // AND_Gate
  and A_prime_C__D_prime (A_prime_C__D_prime_out, ~A, C, ~D);  // AND_Gate
  and A_B_prime_C_prime (A_B_prime_C_prime_out, A, ~B, ~C);  // AND_Gate
  or or_1 (out_5, A_prime_B_prime_C_out, A_prime_B_C_prime_out, A_prime_C__D_prime_out, A_B_prime_C_prime_out);
endmodule

module _7447 (
  input  A,
  input  B,
  input  C,
  input  D,
  output out_5,
  output out_6,
  output out_7,
  output out_8,
  output out_9,
  output out_10,
  output out_11
);

  LedA u_A (.A(A), .B(B), .C(C), .D(D), .out_5(out_5));
  LedB u_B (.A(A), .B(B), .C(C), .D(D), .out_5(out_6));
  LedC u_C (.A(A), .B(B), .C(C), .D(D), .out_5(out_7));
  LedD u_D (.A(A), .B(B), .C(C), .D(D), .out_5(out_8));
  LedE E (.A(A), .B(B), .C(C), .D(D), .out_5(out_9));
  LedF F (.A(A), .B(B), .C(C), .D(D), .out_5(out_10));
  LedG G (.A(A), .B(B), .C(C), .D(D), .out_5(out_11));
endmodule
